// Digital circuit SumadorRestador.dig as structural Verilog
module SumadorRestador (
  input  A0,
  input  B0,
  input  A1,
  input  A2,
  input  A3,
  input  B1,
  input  B2,
  input  B3,
  input  Cin,
  output S0,
  output S1,
  output S2,
  output S3,
  output Cout
);

  wire and_1_out, and_2_out, and_3_out, and_4_out, and_5_out, and_6_out, and_7_out, and_8_out, and_9_out,
       and_10_out, and_11_out, and_12_out, or_1_out, or_2_out, or_3_out, or_4_out, xnor_1_out, xnor_3_out,
       xnor_5_out, xnor_7_out, xor_2_out, xor_3_out, xor_4_out, xor_5_out;

  and and_1 (and_1_out, xor_2_out, or_2_out);
  and and_2 (and_2_out, A3, or_2_out);
  or or_1 (or_1_out, and_3_out, and_2_out, and_1_out);
  xor xor_1 (Cout, or_1_out, Cin);
  and and_3 (and_3_out, A3, xor_2_out);
  xor xor_2 (xor_2_out, B3, Cin);
  xnor xnor_1 (xnor_1_out, xor_2_out, A3);
  xnor xnor_2 (S3, or_2_out, xnor_1_out);
  and and_4 (and_4_out, xor_3_out, or_3_out);
  and and_5 (and_5_out, A2, or_3_out);
  or or_2 (or_2_out, and_6_out, and_5_out, and_4_out);
  and and_6 (and_6_out, A2, xor_3_out);
  xor xor_3 (xor_3_out, B2, Cin);
  xnor xnor_3 (xnor_3_out, xor_3_out, A2);
  xnor xnor_4 (S2, or_3_out, xnor_3_out);
  and and_7 (and_7_out, xor_4_out, or_4_out);
  and and_8 (and_8_out, A1, or_4_out);
  or or_3 (or_3_out, and_9_out, and_8_out, and_7_out);
  and and_9 (and_9_out, A1, xor_4_out);
  xor xor_4 (xor_4_out, B1, Cin);
  xnor xnor_5 (xnor_5_out, xor_4_out, A1);
  xnor xnor_6 (S1, or_4_out, xnor_5_out);
  and and_10 (and_10_out, xor_5_out, Cin);
  and and_11 (and_11_out, A0, Cin);
  or or_4 (or_4_out, and_12_out, and_11_out, and_10_out);
  and and_12 (and_12_out, A0, xor_5_out);
  xor xor_5 (xor_5_out, B0, Cin);
  xnor xnor_7 (xnor_7_out, xor_5_out, A0);
  xnor xnor_8 (S0, Cin, xnor_7_out);
endmodule
